# Fritzing sketch 2-to-1 Mux (4 NAND Gates) (saved by Fritzing 0.9.4)
breadboards: 1

parts:
  U1 = 7400 4 x 2 Input NAND Gate [part_number=7400 package="DIP (Dual Inline) [THT]"]
  R2 = Resistor [tolerance=±5% resistance=1k package="0603 [SMD]"]
  R1 = Resistor [tolerance=±5% resistance=1k package="0603 [SMD]"]
  R3 = Resistor [tolerance=±5% resistance=1k package="0603 [SMD]"]
  LED2 = LED - 3mm [color="Orange (612nm)" package="3 mm [THT]"]
  LED1 = LED - 3mm [color="Orange (612nm)" package="3 mm [THT]"]
  LED3 = LED - 3mm [color="Orange (612nm)" package="3 mm [THT]"]
  S1 = Pushbutton [package="[SMD]"]
  S2 = Pushbutton [package="[SMD]"]
  S3 = Pushbutton [package="[SMD]"]
  LED4 = LED - 3mm [color="Orange (612nm)" package="3 mm [THT]"]
  R4 = Resistor [tolerance=±5% resistance=1k package="0603 [SMD]"]

nets:
  N1: U1.A1, U1.A4, U1.B4, R2.Pin_0, S2.Pin_1, S2.Pin_2
  N2: U1.B1, R1.Pin_0, S1.Pin_1, S1.Pin_2
  N3: U1.Q1, U1.Q2
  N4: U1.A2, U1.A3
  N5: U1.B2, R4.Pin_0
  GND: U1.GND, LED2.cathode, LED1.cathode, LED3.cathode, LED4.cathode
  N6: U1.B3, R3.Pin_0, S3.Pin_1, S3.Pin_2
  N7: U1.Q3, U1.Q4
  N8: U1.VDD, S1.Pin_3, S1.Pin_4, S2.Pin_3, S2.Pin_4, S3.Pin_3, S3.Pin_4
  N9: R2.Pin_1, LED2.anode
  N10: R1.Pin_1, LED1.anode
  N11: R3.Pin_1, LED3.anode
  N12: LED4.anode, R4.Pin_1

notes:
  Output Z
  Pink
  Connect to 3.3V on FPGA board
  Connect to GND on FPGA board
  Input A
  Orange
  Input B
  Yellow
  Input C
  Cyan
