# Fritzing sketch 2-to-1 Mux (Eliminate Static-1 Hazards) (saved by Fritzing 0.9.4)
breadboards: 1

parts:
  U1 = 7400 4 x 2 Input NAND Gate [part_number=7400 package="DIP (Dual Inline) [THT]"]
  R3 = Resistor [tolerance=±5% resistance=1k package="0603 [SMD]"]
  R2 = Resistor [tolerance=±5% resistance=1k package="0603 [SMD]"]
  R1 = Resistor [tolerance=±5% resistance=1k package="0603 [SMD]"]
  LED3 = LED - 3mm [color="Orange (612nm)" package="3 mm [THT]"]
  LED1 = LED - 3mm [color="Orange (612nm)" package="3 mm [THT]"]
  LED2 = LED - 3mm [color="Orange (612nm)" package="3 mm [THT]"]
  S1 = Pushbutton [package="[SMD]"]
  S2 = Pushbutton [package="[SMD]"]
  S3 = Pushbutton [package="[SMD]"]
  R4 = Resistor [tolerance=±5% resistance=1k package="0603 [SMD]"]
  LED4 = LED - 3mm [color="Orange (612nm)" package="3 mm [THT]"]
  U2 = 7400 4 x 2 Input NAND Gate [part_number=7400 package="DIP (Dual Inline) [THT]"]

nets:
  N1: U1.A1, U1.A4, U1.B4, R2.Pin_0, S2.Pin_1, S2.Pin_2
  N2: U1.B1, R1.Pin_0, S1.Pin_1, S1.Pin_2, U2.B4
  N3: U1.Q1, U1.Q2
  N4: U1.A2, U1.A3
  N5: U1.B2, U2.Q2, U2.A2
  GND: U1.GND, LED3.cathode, LED1.cathode, LED2.cathode, LED4.cathode, U2.GND
  N6: U1.B3, R3.Pin_0, S3.Pin_1, S3.Pin_2, U2.A4
  N7: U1.Q3, U1.Q4
  VDD: U1.VDD, S1.Pin_3, S1.Pin_4, S2.Pin_3, S2.Pin_4, S3.Pin_3, S3.Pin_4, U2.VDD
  N8: R3.Pin_1, LED3.anode
  N9: R2.Pin_1, LED2.anode
  N10: R1.Pin_1, LED1.anode
  N11: R4.Pin_0, LED4.anode
  N12: R4.Pin_1, U2.A3
  N13: U2.B2, U2.B3
  N14: U2.Q3, U2.Q4

notes:
  Output Z*
  Purple
  Connect to 3.3V on FPGA board
  Connect to GND on FPGA board
  Input A
  Orange
  Input B
  Yellow
  Input C
  Cyan
  Output Z
  Pink
