# Fritzing sketch 4-bit_logic_processor (saved by Fritzing 0.9.4)
breadboards: 3

parts:
  U1 = 74194 4 Bit Bi-Directional Shift Register [part_number=74194 package="DIP16 [THT]"]
  U2 = 74194 4 Bit Bi-Directional Shift Register [part_number=74194 package="DIP16 [THT]"]
  D1 = LED_BARGRAPH_10 [package=led_bargaph_10]
  R1 = Resistor [tolerance=±5% resistance=1k package="2512 [SMD]"]
  R2 = Resistor [tolerance=±5% resistance=1k package="2512 [SMD]"]
  R3 = Resistor [tolerance=±5% resistance=1k package="2512 [SMD]"]
  R4 = Resistor [tolerance=±5% resistance=1k package="2512 [SMD]"]
  R5 = Resistor [tolerance=±5% resistance=1k package="2512 [SMD]"]
  R6 = Resistor [tolerance=±5% resistance=1k package="2512 [SMD]"]
  R7 = Resistor [tolerance=±5% resistance=1k package="2512 [SMD]"]
  R8 = Resistor [tolerance=±5% resistance=1k package="2512 [SMD]"]
  D3 = LED_BARGRAPH_10 [package=led_bargaph_10]
  U3 = 7400 4 x 2 Input NAND Gate [part_number=7400 package="DIP (Dual Inline) [THT]"]
  U4 = 7400 4 x 2 Input NAND Gate [part_number=7400 package="DIP (Dual Inline) [THT]"]
  U5 = 7486 4 x 2 Input XOR Gate [part_number=7486 package="DIP (Dual Inline) [THT]"]
  U6 = 74153 Dual 4:1 MUX [part_number=74153 package="DIP16 [THT]"]
  U7 = 74153 Dual 4:1 MUX [part_number=74153 package="DIP16 [THT]"]
  LoadA = Pushbutton [package="[SMD]"]
  U8 = 7486 4 x 2 Input XOR Gate [part_number=7486 package="DIP (Dual Inline) [THT]"]
  U9 = 7402 4 x 2 Input NOR Gate [part_number=7402 package="DIP (Dual Inline) [THT]"]
  R9 = Resistor [tolerance=±5% resistance=1k package="2512 [SMD]"]
  LoadB = Pushbutton [package="[SMD]"]
  R10 = Resistor [tolerance=±5% resistance=1k package="2512 [SMD]"]
  U10 = 7474 Dual Positive Edge Triggered D Flip Flop [part_number=7474 package="DIP (Dual Inline) [THT]"]
  U11 = 7410 3 x 3 Input NAND Gate [part_number=7410 package="DIP (Dual Inline) [THT]"]
  U12 = 7400 4 x 2 Input NAND Gate [part_number=7400 package="DIP (Dual Inline) [THT]"]
  U13 = 74161 4 Bit Synchronous Up Down Counter [part_number=74161 package="DIP16 [THT]"]

nets:
  3.3V: U1.1, U1.VCC, U2.1, U2.VCC, U3.VDD, U4.VDD, U5.VDD, U6.D0, U6.VCC, U7.VCC, LoadA.Pin_3, LoadA.Pin_4, U8.VDD, U9.VDD, LoadB.Pin_1, LoadB.Pin_2, U10.A1, U10.Q2, U10.VDD, U11.VDD, U12.VDD, U13.VCC
  N1: U1.2, U7.Y0
  N2: U1.3, U2.3
  N3: U1.4, U2.4
  N4: U1.5, U2.5
  N5: U1.6, U2.6
  GND: U1.GND, U2.GND, R1.Pin_1, R2.Pin_1, R3.Pin_1, R4.Pin_1, R5.Pin_1, R6.Pin_1, R7.Pin_1, R8.Pin_1, U3.GND, U4.GND, U5.GND, U6.G0, U6.GND, U7.G1, U7.G0, U7.GND, U8.GND, U9.GND, R9.Pin_1, R10.Pin_1, U10.GND, U11.GND, U12.GND, U13.GND
  N6: U1.9, U8.Q4
  N7: U1.10, U8.B4, U9.B4
  N8: U1.11, U2.11, U10.Q1, U13.2
  N9: U1.12, D1.G_A, U3.A1, U4.A1, U4.B1, U5.A1, U7.A0, U7.B0, U7.D1
  N10: U1.13, D1.F_A
  N11: U1.14, D1.E_A
  N12: U1.15, D1.D_A
  N13: U2.2, U7.Y1
  N14: U2.9, U8.A3
  N15: U2.10, U8.Q3, U9.Q3
  N16: U2.12, D3.G_A, U3.B1, U4.Q2, U4.A2, U5.B1, U7.D0, U7.C1, U7.A1
  N17: U2.13, D3.F_A
  N18: U2.14, D3.E_A
  N19: U2.15, D3.D_A
  N20: D1.G_C, R1.Pin_0
  N21: D1.F_C, R2.Pin_0
  N22: D1.E_C, R3.Pin_0
  N23: D1.D_C, R4.Pin_0
  N24: R5.Pin_0, D3.G_C
  N25: R6.Pin_0, D3.F_C
  N26: R7.Pin_0, D3.E_C
  N27: R8.Pin_0, D3.D_C
  N28: U3.Q1, U3.Q2, U3.A2
  N29: U3.B2, U6.A0
  N30: U4.Q1, U4.Q3
  N31: U4.B2, U4.B3
  N32: U4.A3, U6.B0
  N33: U5.Q1, U6.C0
  N34: U5.Q4, U7.C0, U7.B1
  N35: U5.B4, U6.Y0
  N36: LoadA.Pin_1, LoadA.Pin_2, U9.B1, U9.Q1, R9.Pin_0
  N37: U8.B3, U8.A4, U11.A3, U13.7, U13.10
  N38: U9.A1, U9.Q4
  N39: U9.Q2, U9.A3
  N40: U9.A2, U9.B2, LoadB.Pin_3, LoadB.Pin_4, R10.Pin_0
  N41: U9.B3, U9.A4, U12.B3, U12.Q3, U12.A4
  N42: U10.B1, U11.B2
  N43: U10.B2, U12.B4
  N44: U11.Q1, U12.A3
  N45: U11.Q2, U11.Q4, U12.Q1
  N46: U11.A2, U11.Q3, U12.B2
  N47: U11.B3, U12.Q4
  N48: U12.A1, U12.B1, U13.14
  N49: U12.Q2, U12.A2, U13.13

notes:
  CLK
  F2
  F1
  F0
  R1
  R0
  D3
  D2
  C
  D0
  FPGA Vcc 3.3V
  FPGA GND
  LoadA
  LoadB
  LED A
  LED B
  E

custom parts:
  74153 Dual 4:1 MUX: 74153 Dual 4:1 Multiplexor
  7410 3 x 3 Input NAND Gate: 7410 3 x 2 Input NAND Gate
