# Fritzing sketch CPU_Trash (saved by Fritzing 0.9.4)
breadboards: 3

parts:
  U2 = 74194 4 Bit Bi-Directional Shift Register [part_number=74194 package="DIP16 [THT]"]
  D1 = LED_BARGRAPH_10 [package=led_bargaph_10]
  D2 = LED_BARGRAPH_10 [package=led_bargaph_10]
  R1 = Resistor [tolerance=±5% resistance=1k package="1206 [SMD]"]
  R2 = Resistor [tolerance=±5% resistance=1k package="1206 [SMD]"]
  R3 = Resistor [tolerance=±5% resistance=1k package="1206 [SMD]"]
  R4 = Resistor [tolerance=±5% resistance=1k package="1206 [SMD]"]
  R5 = Resistor [tolerance=±5% resistance=1k package="1206 [SMD]"]
  R6 = Resistor [tolerance=±5% resistance=1k package="1206 [SMD]"]
  R7 = Resistor [tolerance=±5% resistance=1k package="1206 [SMD]"]
  R8 = Resistor [tolerance=±5% resistance=1k package="1206 [SMD]"]
  U4 = 7400 4 x 2 Input NAND Gate [part_number=7400 package="DIP (Dual Inline) [THT]"]
  U5 = 7486 4 x 2 Input XOR Gate [part_number=7486 package="DIP (Dual Inline) [THT]"]
  U6 = 74153 Dual 4:1 MUX [part_number=74153 package="DIP16 [THT]"]
  U7 = 74153 Dual 4:1 MUX [part_number=74153 package="DIP16 [THT]"]
  U8 = 7402 4 x 2 Input NOR Gate [part_number=7402 package="DIP (Dual Inline) [THT]"]
  LoadA = Pushbutton [package="[SMD]"]
  LoadB = Pushbutton [package="[SMD]"]
  R9 = Resistor [tolerance=±5% resistance=220 package="1206 [SMD]"]
  R10 = Resistor [tolerance=±5% resistance=220 package="1206 [SMD]"]
  U9 = 7474 Dual Positive Edge Triggered D Flip Flop [part_number=7474 package="DIP (Dual Inline) [THT]"]
  U10 = 7410 3 x 3 Input NAND Gate [part_number=7410 package="DIP (Dual Inline) [THT]"]
  U11 = 7400 4 x 2 Input NAND Gate [part_number=7400 package="DIP (Dual Inline) [THT]"]
  U12 = 74161 4 Bit Synchronous Up Down Counter [part_number=74161 package="DIP16 [THT]"]
  U13 = 7486 4 x 2 Input XOR Gate [part_number=7486 package="DIP (Dual Inline) [THT]"]
  U1 = 74194 4 Bit Bi-Directional Shift Register [part_number=74194 package="DIP16 [THT]"]
  U3 = 7400 4 x 2 Input NAND Gate [part_number=7400 package="DIP (Dual Inline) [THT]"]

nets (from the schematic view):
  3.3V: U2.1, U2.VCC, U4.VDD, U5.VDD, U6.D0, U6.VCC, U7.VCC, U8.VDD, LoadA.Pin_1, LoadA.Pin_2, LoadB.Pin_1, LoadB.Pin_2, U9.A1, U9.Q2, U9.VDD, U10.VDD, U11.VDD, U12.VCC, U13.VDD, U1.1, U1.VCC, U3.VDD
  N1: U2.2, U7.Y1
  D: U2.3, U1.3
  C: U2.4, U1.4
  B: U2.5, U1.5
  A: U2.6, U1.6
  GND: U2.GND, R1.Pin_0, R2.Pin_0, R3.Pin_0, R4.Pin_0, R5.Pin_0, R6.Pin_0, R7.Pin_0, R8.Pin_0, U5.GND, U6.G0, U6.GND, U7.G1, U7.G0, U7.GND, R9.Pin_1, R10.Pin_1, U9.GND, U10.GND, U11.GND, U12.GND, U13.GND, U1.GND, U3.GND
  N2: U2.9, U13.B2
  N3: U2.10, U8.Q3, U13.Q2
  CLK: U2.11, U9.Q1, U12.2, U1.11
  N4: U2.12, D2.D_A, U4.Q2, U4.A2, U5.B1, U7.D0, U7.C1, U7.A1, U3.B1
  N5: U2.13, D2.C_A
  N6: U2.14, D2.B_A
  N7: U2.15, D2.A_A
  N8: D1.A_A, U1.15
  N9: D1.B_A, U1.14
  N10: D1.C_A, U1.13
  N11: D1.D_A, U4.A1, U4.B1, U5.A1, U7.A0, U7.B0, U7.D1, U1.12, U3.A1
  N12: D1.D_C, R4.Pin_1
  N13: D1.C_C, R3.Pin_1
  N14: D1.B_C, R2.Pin_1
  N15: D1.A_C, R1.Pin_1
  N16: D2.D_C, R8.Pin_1
  N17: D2.C_C, R7.Pin_1
  N18: D2.B_C, R6.Pin_1
  N19: D2.A_C, R5.Pin_1
  N20: U4.Q1, U4.Q3
  N21: U4.B2, U4.B3
  N22: U4.A3, U6.B0
  N23: U5.Q1, U6.C0
  F2: U5.Q2
  N24: U5.A2, U6.Y0
  N25: U5.B2, U7.C0, U7.B1
  F1: U6.S1
  N26: U6.A0, U3.A2
  F0: U6.S0
  N27: U7.Y0, U1.2
  R1: U7.S1
  R0: U7.S0
  N28: U8.A1, U8.A4
  N29: U8.B1, U8.Q1, LoadA.Pin_3, LoadA.Pin_4, R9.Pin_0
  N30: U8.Q2, U8.A3
  N31: U8.A2, U8.B2, LoadB.Pin_3, LoadB.Pin_4, R10.Pin_0
  E: U8.B3, U8.Q4, U11.Q3, U11.A4, U11.B4
  N32: U8.B4, U13.A1, U1.10
  N33: U9.B1, U10.B2
  N34: U9.B2, U11.B3
  N35: U10.Q1, U11.Q4
  N36: U10.Q2, U10.B3, U11.B2
  N37: U10.A2, U10.Q3, U11.Q1
  N38: U10.A3, U12.7, U12.10, U13.B1
  N39: U10.Q4, U11.A3
  N40: U11.A1, U11.B1, U12.14
  N41: U11.Q2, U11.A2, U12.13
  N42: U13.Q1, U1.9
  N43: U3.Q1, U3.Q2

custom parts:
  74153 Dual 4:1 MUX: 74153 Dual 4:1 Multiplexor
  7410 3 x 3 Input NAND Gate: 7410 3 x 2 Input NAND Gate
